# Fritzing sketch BIM iot Conference (saved by Fritzing 0.9.6b)
breadboards: 1

parts:
  U1 = NodeMCU V1.0
  M1 = MAX30102
  OLED_I2C1 = OLED 128x64 I2C Monochrome Display
  Mod2 = gy-906
  U3 = LM2596 step down module
  BATT1 = LiPoly Battery (1300mAh)
  Part1 = RFID-RC522-v3
  J1 = Basic Servo
  Mod3 = ESP32 - CAM
  M3 = fc-51 [package=THT]

nets:
  N1: U1.D1, M1.SCL, OLED_I2C1.SCK, Mod2.SCL
  N2: U1.D2, M1.SDA, OLED_I2C1.SDA, Mod2.SDA
  N3: U1.D3, Part1.RST
  N4: U1.D4, Part1.SDA
  3V3: U1.3V3, Part1.3.3V, Mod3.VCC
  GND: U1.GND, M1.GND, Mod2.GND, U3.IN-, U3.OUT-, BATT1.negative, Part1.GND, J1.gnd, Mod3.GND, M3.pin2
  N5: U1.D5, Part1.SCK
  N6: U1.D6, Part1.MISO
  N7: U1.D7, Part1.MOSI
  N8: U1.A0, J1.pulse, M3.pin1
  VIN: M1.VIN, OLED_I2C1.VDD, Mod2.VIN, U3.OUT+, J1.vcc, M3.pin3
  N9: U3.IN+, BATT1.positive

custom parts:
  NodeMCU V1.0: ESP8266 based NodeMCU
  MAX30102: Oximeter module using the MAX30102 chip. You may wish to read (and check your module) this post on power problems with these modules: https://reedpaper.wordpress.com/2018/08/22/pulse-oximeter-max30100-max30102-how-to-fix-wrong-board/ . As usual, if you want the mounting holes in pcb, you need to drag a hole over the pad in silkscreen to actually drill the hole (by default they are not drilled)
  gy-906: gy-906 Non-contact PIR I2C interface temperature sensor breakout board.
  LM2596 step down module: LM2596 DC-DC step down power supply module 3 A.
  LiPoly Battery (1300mAh): Lithium Ion Polymer Battery (1300mAh)
  RFID-RC522-v3: A simple China made RFID-RC522 Reader (6x4 cm); do check the pin labels, as this is a MFRC522 based clone.
  ESP32 - CAM: The ESP32-CAM has a very competitive small-size camera module that can operate independently as a minimum system with a footprint of only 27*40.5*4.5mm and a deep sleep current of up to 6mA.
